# Fritzing sketch Breadboard_setup (saved by Fritzing 1.0.6)
circuit board: 9.12935cm x 3.87765cm
breadboards: 1

parts:
  A1 = Teensy 4.1
  SparkFun_IMU_Breakout_ICM-1 = SparkFun IMU Breakout ICM-20948 [part_number=15335]

nets:
  N1: A1.Pin_12, A1.Pin_50, A1.Pin_63, SparkFun_IMU_Breakout_ICM-1.GND
  N2: A1.Pin_26, A1.Pin_62, SparkFun_IMU_Breakout_ICM-1.VIN
  N3: A1.Pin_56, SparkFun_IMU_Breakout_ICM-1.SDA/SDI_VIN
  N4: A1.Pin_57, SparkFun_IMU_Breakout_ICM-1.SCL/SCLK_VIN

custom parts:
  Teensy 4.1: The Teensy is a complete USB-based microcontoller development system, in a very small footprint, capable of implementing many types of projects. All programming is done via the USB port. No special programmer is needed, only a standard micro-USB cable and a PC or Macintosh with a USB port.
  SparkFun IMU Breakout ICM-20948: The SparkFun 9DoF IMU Breakout incorporates all the amazing features of Invensense's ICM-20948 into a Qwiic-enabled breakout board complete with a logic shifter and broken out GPIO pins for all your motion sensing needs. The ICM-20948 itself is an extremely low powered, I2C and SPI enabled 9-axis motion tracking device that is ideally suited for smartphones, tablets, wearable sensors, and IoT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
